# Fritzing sketch temp_probe_proto_shield (saved by Fritzing 0.9.2b)

parts:
  R2 = Resistor [tolerance=±5% resistance=10k package=THT]
  R1 = Resistor [tolerance=±5% resistance=10k package=THT]
  R3 = Resistor [tolerance=±5% resistance=10k package=THT]
  R4 = Resistor [tolerance=±5% resistance=10k package=THT]
  R5 = Resistor [tolerance=±5% resistance=10k package=THT]
  R6 = Resistor [tolerance=±5% resistance=10k package=THT]
  RHT3 = Humidity and Temperature Sensor RHT03
  RHT4 = Humidity and Temperature Sensor RHT03
  RHT5 = Humidity and Temperature Sensor RHT03
  RHT6 = Humidity and Temperature Sensor RHT03
  RHT2 = Humidity and Temperature Sensor RHT03
  RHT1 = Humidity and Temperature Sensor RHT03
  J1 = Generic male header - 3 pins [form="♀ (female)" package=THT]
  Part2 = Adafruit Proto Shield for Arduino Kit - v.5
  J2 = Generic male header - 3 pins [form="♀ (female)" package=THT]
  J3 = Generic male header - 3 pins [form="♀ (female)" package=THT]
  J4 = Generic male header - 3 pins [form="♀ (female)" package=THT]
  J5 = Generic male header - 3 pins [form="♀ (female)" package=THT]
  J6 = Generic male header - 3 pins [form="♀ (female)" package=THT]

nets:
  N1: R2.Pin_0, RHT5.Data-signal, Part2.D3, Part2.1#143, Part2.P$5#144, Part2.P$6#145, Part2.N$111, J2.Pin_2
  VCC: R2.Pin_1, R1.Pin_1, R3.Pin_1, R4.Pin_1, R5.Pin_1, R6.Pin_1, RHT3.Vcc, RHT4.Vcc, RHT5.Vcc, RHT6.Vcc, RHT2.Vcc, RHT1.Vcc, J1.Pin_1, Part2.+5V, Part2.P$2, Part2.P$4, Part2.P$6#232, Part2.P$8, Part2.P$10, Part2.P$11#237, Part2.N$31, Part2.N$47, Part2.N$96, Part2.N$112, Part2.N$161, Part2.N$242, J2.Pin_1, J3.Pin_1, J4.Pin_1, J5.Pin_1, J6.Pin_1
  N2: R1.Pin_0, Part2.N$140
  N3: R3.Pin_0, RHT4.Data-signal, Part2.D4, Part2.1#152, Part2.P$5#153, Part2.P$6#154, Part2.N$95, J3.Pin_2
  N4: R4.Pin_0, RHT3.Data-signal, Part2.D5, Part2.1#166, Part2.P$5#167, Part2.P$6#168, Part2.N$46, J4.Pin_2
  N5: R5.Pin_0, RHT2.Data-signal, Part2.D6, Part2.1#163, Part2.P$5#164, Part2.P$6#165, Part2.N$30, J5.Pin_2
  N6: R6.Pin_0, RHT1.Data-signal, Part2.D7, Part2.1#156, Part2.P$5#157, Part2.P$6#158, Part2.N$241, J6.Pin_2
  N7: RHT3.GND_2, RHT4.GND_2, RHT5.GND_2, RHT6.GND_2, RHT2.GND_2, RHT1.GND_2, J1.Pin_3, Part2.P$3, Part2.P$5#20, Part2.P$7, Part2.P$9, Part2.P$11#26, Part2.P$12, Part2.GND, Part2.N$22, J2.Pin_3, J3.Pin_3, J4.Pin_3, J5.Pin_3, J6.Pin_3
  N8: RHT6.Data-signal, J1.Pin_2, Part2.N$138, Part2.N$160
  N9: Part2.D2, Part2.N$139

custom parts:
  Generic male header - 3 pins: Generic male header
  Adafruit Proto Shield for Arduino Kit - v.5: Arduino prototyping shield designed by Adafruit Industries
